// Logisim project lastname_firstname.circ as structural Verilog: 7 circuits, main circuit main
module main (
);

  wire A, AddOff, B, Branch, Clock, EnOFF, FuncHi, FuncLo, RdMem, ReadR2, RegDataHi, RegDataLo, RegToWr,
       WrMem, WrReg;
  wire [1:0] Reg2;
  wire [2:0] Opcode;
  wire [3:0] multiplexer_2_out, Rx, Ry, Rz;
  wire [7:0] PC_q, PC_q_2, PC_q_3, PC_q_4;
  wire [19:4] undriven;
  wire [31:0] adder_1_out, multiplexer_1_out, rom_1_data;

  Register #(.width(32)) PC (
    .D(multiplexer_1_out), .en(1'b1), .Q({PC_q, PC_q_4, PC_q_3, PC_q_2}), .clk(Clock));  // open: clr
  Clock clock_1 (.out(Clock));
  Multiplexer #(.select(2), .width(32)) multiplexer_1 (
    .in0(adder_1_out), .out(multiplexer_1_out), .en(1'b1));  // open: in1, in2, in3, sel
  Adder #(.width(32)) adder_1 (.a({PC_q, PC_q_4, PC_q_3, PC_q_2}), .b(32'h1), .out(adder_1_out));  // open: cin, cout
  ROM #(.addrWidth(24), .dataWidth(32)) rom_1 (.addr({PC_q_4, PC_q_3, PC_q_2}), .data(rom_1_data));  // open: sel
  Controlled_Buffer #(.width(20)) controlled_buffer_1 (.in({undriven, Rz}), .en(EnOFF));  // open: out
  ROM #(.addrWidth(3), .dataWidth(12)) rom_2 (
    .addr(Opcode),
    .data({RegDataLo, RegDataHi, WrReg, WrMem, RdMem, Branch, AddOff, FuncLo, FuncHi, RegToWr, B, A}));  // open: sel
  Multiplexer #(.select(2), .width(4)) multiplexer_2 (
    .in0(Rx), .in1(Ry), .in2(Rz), .out(multiplexer_2_out), .sel(Reg2), .en(ReadR2));  // open: in3
  Dual_Ported_Register_File dual_ported_register_file_1 (
    .CLK(Clock), .RdREGNO1(Ry), .RdREGNO2(multiplexer_2_out));  // open: WrREGNO, INPUT, OUT1, OUT2, WrEN

  // Notes on the sheet:
  //   contents of rom_2 (hex, n*v repeats v):
  //   1
endmodule

module Dual_Ported_Register_File (
  input  CLK,
  input  WrEN,
  input  [3:0] WrREGNO,
  input  [3:0] RdREGNO1,
  input  [3:0] RdREGNO2,
  input  [31:0] INPUT,
  output [31:0] OUT1,
  output [31:0] OUT2
);

  wire En_a0, En_a1, En_a2, En_a3, En_a4, En_at, En_fp, En_k0, En_ra, En_s0, En_s1, En_s2, En_s3, En_sp,
       En_v0;
  wire [31:0] a0, a1, a2, a3, a4, at, fp, k0, ra, s0, s1, s2, s3, sp, v0, zero;

  Decoder #(.select(4), .disabled(0)) decoder_1 (
    .out1(En_at), .out2(En_v0), .out3(En_a0), .out4(En_a1), .out5(En_a2), .out6(En_a3), .out7(En_a4),
    .out8(En_s0), .out9(En_s1), .out10(En_s2), .out11(En_s3), .out12(En_k0), .out13(En_sp), .out14(En_fp),
    .out15(En_ra), .sel(WrREGNO), .en(WrEN));  // open: out0
  Register #(.width(32)) u_zero (.D(INPUT), .en(1'b0), .Q(zero), .clk(CLK));  // open: clr
  Register #(.width(32)) u_at (.D(INPUT), .en(En_at), .Q(at), .clk(CLK));  // open: clr
  Register #(.width(32)) u_v0 (.D(INPUT), .en(En_v0), .Q(v0), .clk(CLK));  // open: clr
  Register #(.width(32)) u_a0 (.D(INPUT), .en(En_a0), .Q(a0), .clk(CLK));  // open: clr
  Register #(.width(32)) u_a1 (.D(INPUT), .en(En_a1), .Q(a1), .clk(CLK));  // open: clr
  Register #(.width(32)) u_a2 (.D(INPUT), .en(En_a2), .Q(a2), .clk(CLK));  // open: clr
  Register #(.width(32)) u_a3 (.D(INPUT), .en(En_a3), .Q(a3), .clk(CLK));  // open: clr
  Register #(.width(32)) u_a4 (.D(INPUT), .en(En_a4), .Q(a4), .clk(CLK));  // open: clr
  Multiplexer #(.select(4), .width(32), .disabled(0), .enable("false")) multiplexer_1 (
    .in0(zero), .in1(at), .in2(v0), .in3(a0), .in4(a1), .in5(a2), .in6(a3), .in7(a4), .in8(s0), .in9(s1),
    .in10(s2), .in11(s3), .in12(k0), .in13(sp), .in14(fp), .in15(ra), .out(OUT2), .sel(RdREGNO2));
  Register #(.width(32)) u_s0 (.D(INPUT), .en(En_s0), .Q(s0), .clk(CLK));  // open: clr
  Register #(.width(32)) u_s1 (.D(INPUT), .en(En_s1), .Q(s1), .clk(CLK));  // open: clr
  Register #(.width(32)) u_s2 (.D(INPUT), .en(En_s2), .Q(s2), .clk(CLK));  // open: clr
  Register #(.width(32)) u_s3 (.D(INPUT), .en(En_s3), .Q(s3), .clk(CLK));  // open: clr
  Register #(.width(32)) u_k0 (.D(INPUT), .en(En_k0), .Q(k0), .clk(CLK));  // open: clr
  Register #(.width(32)) u_sp (.D(INPUT), .en(En_sp), .Q(sp), .clk(CLK));  // open: clr
  Register #(.width(32)) u_fp (.D(INPUT), .en(En_fp), .Q(fp), .clk(CLK));  // open: clr
  Register #(.width(32)) u_ra (.D(INPUT), .en(En_ra), .Q(ra), .clk(CLK));  // open: clr
  Multiplexer #(.select(4), .width(32), .disabled(0), .enable("false")) multiplexer_2 (
    .in0(zero), .in1(at), .in2(v0), .in3(a0), .in4(a1), .in5(a2), .in6(a3), .in7(a4), .in8(s0), .in9(s1),
    .in10(s2), .in11(s3), .in12(k0), .in13(sp), .in14(fp), .in15(ra), .out(OUT1), .sel(RdREGNO1));

  // Notes on the sheet:
  //   MODIFY AT YOUR OWN RISK
endmodule

module IF_IDRR_Buffer (
  input  [31:0] Instruction_In,
  input  Clock,
  input  [31:0] PC_In,
  output [31:0] Instruction_Out,
  output [31:0] PC_Out
);

  Register #(.width(32)) register_1 (.D(Instruction_In), .en(1'b1), .Q(Instruction_Out), .clk(Clock));  // open: clr
  Register #(.width(32)) register_2 (.D(PC_In), .en(1'b1), .Q(PC_Out), .clk(Clock));  // open: clr
endmodule

module IDRR_EX_Buffer (
  input  [31:0] A_In,
  input  [31:0] B_In,
  input  Clock,
  input  [31:0] Off_In,
  input  [31:0] PC_In,
  input  [3:0] Rx_In,
  output [31:0] A_Out,
  output [31:0] B_Out,
  output [31:0] Off_Out,
  output [31:0] PC_Out,
  output [3:0] Rx_Out
);

  wire undriven, undriven_2, undriven_3, undriven_4, undriven_5;

  Register #(.width(32)) register_1 (.D(A_In), .en(undriven), .Q(A_Out), .clk(Clock));  // open: clr
  Register #(.width(32)) register_2 (.D(B_In), .en(undriven_2), .Q(B_Out), .clk(Clock));  // open: clr
  Register #(.width(32)) register_3 (.D(Off_In), .en(undriven_3), .Q(Off_Out), .clk(Clock));  // open: clr
  Register #(.width(32)) register_4 (.D(PC_In), .en(undriven_4), .Q(PC_Out), .clk(Clock));  // open: clr
  Register #(.width(4)) register_5 (.D(Rx_In), .en(undriven_5), .Q(Rx_Out), .clk(Clock));  // open: clr
endmodule

module EX_MEM_Buffer (
  input  [3:0] Opcode_In,
  input  Enable_Op,
  input  [3:0] Rx_In,
  input  Enable_Rx,
  input  Clock,
  input  [31:0] ALU1_In,
  input  Enable_ALU1,
  input  [31:0] ALU2_In,
  input  Enable_ALU2,
  output [3:0] Opcode_Out,
  output [3:0] Rx_Out,
  output [31:0] ALU1_Out,
  output [31:0] ALU2_Out
);

  Register #(.width(4)) register_1 (.D(Opcode_In), .en(Enable_Op), .Q(Opcode_Out), .clk(Clock));  // open: clr
  Register #(.width(4)) register_2 (.D(Rx_In), .en(Enable_Rx), .Q(Rx_Out), .clk(Clock));  // open: clr
  Register #(.width(32)) register_3 (.D(ALU1_In), .en(Enable_ALU1), .Q(ALU1_Out), .clk(Clock));  // open: clr
  Register #(.width(32)) register_4 (.D(ALU2_In), .en(Enable_ALU2), .Q(ALU2_Out), .clk(Clock));  // open: clr
endmodule

module MEM_WB_Buffer (
  input  [3:0] Opcode_In,
  input  Enable_Op,
  input  [3:0] Rx_In,
  input  Enable_Rx,
  input  Clock,
  input  [31:0] ALU1_In,
  input  Enable_ALU1,
  input  [31:0] ALU2_In,
  input  Enable_ALU2,
  input  [31:0] D_MEM_In,
  input  Enable_D_MEM,
  output [3:0] Opcode_Out,
  output [3:0] Rx_Out,
  output [31:0] ALU1_Out,
  output [31:0] ALU2_Out,
  output [31:0] D_MEM_Out
);

  Register #(.width(4)) register_1 (.D(Opcode_In), .en(Enable_Op), .Q(Opcode_Out), .clk(Clock));  // open: clr
  Register #(.width(4)) register_2 (.D(Rx_In), .en(Enable_Rx), .Q(Rx_Out), .clk(Clock));  // open: clr
  Register #(.width(32)) register_3 (.D(ALU1_In), .en(Enable_ALU1), .Q(ALU1_Out), .clk(Clock));  // open: clr
  Register #(.width(32)) register_4 (.D(ALU2_In), .en(Enable_ALU2), .Q(ALU2_Out), .clk(Clock));  // open: clr
  Register #(.width(32)) register_5 (.D(D_MEM_In), .en(Enable_D_MEM), .Q(D_MEM_Out), .clk(Clock));  // open: clr
endmodule

module ALU (
  input  [1:0] FUNC,
  input  [31:0] A,
  input  [31:0] B,
  output [31:0] OUT
);

  wire [31:0] adder_1_out, adder_2_out, nand_1_out, subtractor_1_out;

  Adder #(.width(32)) adder_1 (.a(A), .b(B), .out(adder_1_out), .cin(1'b0));  // open: cout
  assign nand_1_out = ~(A & B);  // NAND_Gate nand_1, 32 bits wide
  Subtractor #(.width(32)) subtractor_1 (.a(A), .b(B), .out(subtractor_1_out), .bin(1'b0));  // open: bout
  Adder #(.width(32)) adder_2 (.a(A), .b({32{1'b0}}), .out(adder_2_out), .cin(1'b1));  // open: cout
  Multiplexer #(.select(2), .width(32), .disabled(0), .enable("false")) multiplexer_1 (
    .in0(adder_1_out), .in1(nand_1_out), .in2(subtractor_1_out), .in3(adder_2_out), .out(OUT), .sel(FUNC));

  // Notes on the sheet:
  //   MODIFY AT YOUR OWN RISK
endmodule
